// Logisim project task2.2.circ as structural Verilog
module dlatchtest (
  input  in_1,
  input  in_2,
  output Q,
  output Q_prime
);

  wire and_1_out, and_2_out, not_1_out;

  not not_1 (not_1_out, in_2);
  and and_1 (and_1_out, in_1, not_1_out);
  and and_2 (and_2_out, in_1, in_2);
  nor nor_1 (Q, and_1_out, Q_prime);
  nor nor_2 (Q_prime, Q, and_2_out);
endmodule

module d_flipflop (
  input  CLK,
  input  Din,
  output Q
);

  wire dlatchtest_1_q, not_1_out;

  not not_1 (not_1_out, CLK);
  dlatchtest dlatchtest_1 (.in_1(not_1_out), .in_2(Din), .Q(dlatchtest_1_q));  // open: Q_prime
  dlatchtest dlatchtest_2 (.in_1(CLK), .in_2(dlatchtest_1_q), .Q(Q));  // open: Q_prime
endmodule

module d_register (
  input  [3:0] in_1,
  output [3:0] out_2
);

  wire clock_1_out;

  Clock clock_1 (.out(clock_1_out));
  d_flipflop d_flipflop_1 (.Din(in_1[0]), .CLK(clock_1_out), .Q(out_2[0]));
  d_flipflop d_flipflop_2 (.Din(in_1[1]), .CLK(clock_1_out), .Q(out_2[1]));
  d_flipflop d_flipflop_3 (.Din(in_1[2]), .CLK(clock_1_out), .Q(out_2[2]));
  d_flipflop d_flipflop_4 (.Din(in_1[3]), .CLK(clock_1_out), .Q(out_2[3]));
endmodule

module register (
  input  [3:0] X,
  output [3:0] Y
);

  wire clock_1_out;

  Clock clock_1 (.out(clock_1_out));
  d_flipflop d_flipflop_1 (.Din(X[0]), .CLK(clock_1_out), .Q(Y[0]));
  d_flipflop d_flipflop_2 (.Din(X[1]), .CLK(clock_1_out), .Q(Y[1]));
  d_flipflop d_flipflop_3 (.Din(X[2]), .CLK(clock_1_out), .Q(Y[2]));
  d_flipflop d_flipflop_4 (.Din(X[3]), .CLK(clock_1_out), .Q(Y[3]));
endmodule

module dj (
  input  in_1
);
endmodule
